// Logisim project exper2.circ as structural Verilog
module \题目1  (
  input  Ci1,
  input  Ai,
  input  Bi,
  output Si,
  output Ci
);

  wire and_1_out, and_2_out, and_3_out, and_4_out, and_5_out, and_6_out, and_7_out, not_1_out, not_2_out,
       not_3_out, not_4_out, not_5_out, not_6_out;

  not not_1 (not_1_out, Ci1);
  not not_2 (not_2_out, Ai);
  not not_3 (not_3_out, Ci1);
  not not_4 (not_4_out, Bi);
  not not_5 (not_5_out, Ai);
  not not_6 (not_6_out, Bi);
  and and_1 (and_1_out, Ai, Bi);
  and and_2 (and_2_out, Ci1, Bi);
  and and_3 (and_3_out, Ci1, Ai);
  and and_4 (and_4_out, not_1_out, not_2_out, Bi);
  and and_5 (and_5_out, not_3_out, Ai, not_4_out);
  and and_6 (and_6_out, Ci1, not_5_out, not_6_out);
  and and_7 (and_7_out, Ci1, Ai, Bi);
  or or_1 (Ci, and_1_out, and_2_out, and_3_out);
  or or_2 (Si, and_4_out, and_5_out, and_6_out, and_7_out);
endmodule

module \题目6  (
  input  a,
  input  b,
  input  c,
  output s1,
  output s2
);

  wire and_1_out, and_2_out, and_3_out, and_4_out, and_5_out, and_6_out, and_7_out, and_8_out, not_1_out,
       not_2_out, not_3_out, not_4_out, not_5_out, not_6_out, not_7_out, not_8_out, not_9_out, not_10_out,
       not_11_out, not_12_out;

  not not_1 (not_1_out, a);
  not not_2 (not_2_out, b);
  not not_3 (not_3_out, a);
  not not_4 (not_4_out, c);
  not not_5 (not_5_out, b);
  not not_6 (not_6_out, c);
  not not_7 (not_7_out, a);
  not not_8 (not_8_out, b);
  not not_9 (not_9_out, c);
  not not_10 (not_10_out, a);
  not not_11 (not_11_out, b);
  not not_12 (not_12_out, c);
  and and_1 (and_1_out, not_1_out, not_2_out, c);
  and and_2 (and_2_out, not_3_out, b, not_4_out);
  and and_3 (and_3_out, a, not_5_out, not_6_out);
  and and_4 (and_4_out, a, b, c);
  and and_5 (and_5_out, not_7_out, b, c);
  and and_6 (and_6_out, a, not_8_out, c);
  and and_7 (and_7_out, a, b, not_9_out);
  and and_8 (and_8_out, not_10_out, not_11_out, not_12_out);
  or or_1 (s1, and_1_out, and_2_out, and_3_out, and_4_out);
  or or_2 (s2, and_5_out, and_6_out, and_7_out, and_8_out);
endmodule

module test (
  input  a,
  input  b,
  output sum,
  output cout
);

  and and_1 (cout, a, b);
  xor xor_1 (sum, a, b);
endmodule

module \题目2  (
  input  A0,
  input  A1,
  input  A2,
  input  G1,
  input  G2,
  input  G3,
  output Y0,
  output Y1,
  output Y2,
  output Y3,
  output Y4,
  output Y5,
  output Y6,
  output Y7
);

  wire not_1_out, not_2_out, not_3_out, not_4_out, not_5_out, not_6_out, not_7_out, not_8_out, not_9_out,
       not_10_out, not_11_out, not_12_out, not_13_out, not_14_out, not_15_out, not_16_out, not_17_out,
       not_18_out, not_19_out, not_20_out;

  not not_1 (not_1_out, G1);
  not not_2 (not_2_out, G1);
  not not_3 (not_3_out, A0);
  not not_4 (not_4_out, G1);
  not not_5 (not_5_out, A1);
  not not_6 (not_6_out, G1);
  not not_7 (not_7_out, A0);
  not not_8 (not_8_out, A1);
  not not_9 (not_9_out, G1);
  not not_10 (not_10_out, A2);
  not not_11 (not_11_out, G1);
  not not_12 (not_12_out, A0);
  not not_13 (not_13_out, A2);
  not not_14 (not_14_out, G1);
  not not_15 (not_15_out, A1);
  not not_16 (not_16_out, A2);
  not not_17 (not_17_out, G1);
  not not_18 (not_18_out, A0);
  not not_19 (not_19_out, A1);
  not not_20 (not_20_out, A2);
  or or_1 (Y0, not_1_out, G2, G3, A0, A1, A2);
  or or_2 (Y1, not_2_out, G2, G3, not_3_out, A1, A2);
  or or_3 (Y2, not_4_out, G2, G3, A0, not_5_out, A2);
  or or_4 (Y3, not_6_out, G2, G3, not_7_out, not_8_out, A2);
  or or_5 (Y4, not_9_out, G2, G3, A0, A1, not_10_out);
  or or_6 (Y5, not_11_out, G2, G3, not_12_out, A1, not_13_out);
  or or_7 (Y6, not_14_out, G2, G3, A0, not_15_out, not_16_out);
  or or_8 (Y7, not_17_out, G2, G3, not_18_out, not_19_out, not_20_out);
endmodule

module Data_Selector (
  input  a,
  input  sel,
  input  b,
  output out
);

  wire and_1_out, and_2_out, not_1_out;

  not not_1 (not_1_out, sel);
  and and_1 (and_1_out, a, not_1_out);
  and and_2 (and_2_out, sel, b);
  or or_1 (out, and_1_out, and_2_out);
endmodule

module MUX4TO1 (
  input  sel0,
  input  sel1,
  input  a,
  input  b,
  input  in_5,
  input  d,
  output out
);

  wire data_selector_1_out, data_selector_2_out;

  Data_Selector data_selector_1 (.a(a), .sel(sel1), .b(b), .out(data_selector_1_out));
  Data_Selector data_selector_2 (.a(in_5), .sel(sel1), .b(d), .out(data_selector_2_out));
  Data_Selector data_selector_3 (.a(data_selector_1_out), .sel(sel0), .b(data_selector_2_out), .out(out));

  // Notes on the sheet:
  //   carry1
  //   carry2
endmodule
