// Logisim project exper3.circ as structural Verilog
module \双稳态  (
  input  R,
  input  S,
  output Q,
  output nQ
);

  nor nor_1 (Q, R, nQ);
  nor nor_2 (nQ, Q, S);
endmodule

module Dlatch (
  input  in_1,
  input  in_2,
  input  in_3,
  output Q,
  output nQ
);

  wire and_1_out, and_2_out, and_3_out, not_1_out, not_2_out, or_1_out;

  not not_1 (not_1_out, and_1_out);
  and and_1 (and_1_out, in_2, in_3);
  not not_2 (not_2_out, in_2);
  and and_2 (and_2_out, in_1, not_1_out);
  and and_3 (and_3_out, in_1, and_1_out);
  or or_1 (or_1_out, not_2_out, and_2_out);
  \双稳态  \u_双稳态_1  (.R(or_1_out), .S(and_3_out), .Q(Q), .nQ(nQ));
endmodule

module Dchufa (
  input  in_1,
  input  in_2,
  input  in_3,
  output out_4,
  output out_5
);

  wire dlatch_1_q, not_1_out;

  not not_1 (not_1_out, in_1);
  Dlatch dlatch_1 (.Q(dlatch_1_q), .in_1(not_1_out), .in_3(in_3), .in_2(in_2));  // open: nQ
  Dlatch dlatch_2 (.Q(out_4), .nQ(out_5), .in_1(in_1), .in_3(dlatch_1_q), .in_2(in_2));
endmodule

module register (
  input  [3:0] in_1,
  input  in_2,
  input  in_3,
  output [3:0] out_4
);

  Dchufanes dchufanes_1 (.in_1(in_2), .in_2(in_1[0]), .in_3(in_3), .out_4(out_4[0]));  // open: out_5
  Dchufanes dchufanes_2 (.in_1(in_2), .in_2(in_1[1]), .in_3(in_3), .out_4(out_4[1]));  // open: out_5
  Dchufanes dchufanes_3 (.in_1(in_2), .in_2(in_1[2]), .in_3(in_3), .out_4(out_4[2]));  // open: out_5
  Dchufanes dchufanes_4 (.in_1(in_2), .in_2(in_1[3]), .in_3(in_3), .out_4(out_4[3]));  // open: out_5
endmodule

module add_4bit (
  input  in_1,
  input  [3:0] in_2,
  input  [3:0] in_3,
  output [3:0] out_4
);

  wire add_1bit_1_out_5, add_1bit_2_out_5, add_1bit_3_out_5;

  add_1bit add_1bit_1 (.in_1(in_2[0]), .in_2(in_3[0]), .in_3(in_1), .out_4(out_4[0]), .out_5(add_1bit_1_out_5));
  add_1bit add_1bit_2 (
    .in_1(in_2[1]), .in_2(in_3[1]), .in_3(add_1bit_1_out_5), .out_4(out_4[1]), .out_5(add_1bit_2_out_5));
  add_1bit add_1bit_3 (
    .in_1(in_2[2]), .in_2(in_3[2]), .in_3(add_1bit_2_out_5), .out_4(out_4[2]), .out_5(add_1bit_3_out_5));
  add_1bit add_1bit_4 (.in_1(in_2[3]), .in_2(in_3[3]), .in_3(add_1bit_3_out_5), .out_4(out_4[3]));  // open: out_5
endmodule

module add_1bit (
  input  in_1,
  input  in_2,
  input  in_3,
  output out_4,
  output out_5
);

  wire and_1_out, and_2_out, and_3_out, or_1_out, xor_1_out;

  xor xor_1 (xor_1_out, in_1, in_2);
  and and_1 (and_1_out, in_1, in_2);
  and and_2 (and_2_out, in_1, in_3);
  and and_3 (and_3_out, in_3, in_2);
  xor xor_2 (out_4, xor_1_out, in_3);
  or or_1 (or_1_out, and_1_out, and_2_out);
  or or_2 (out_5, or_1_out, and_3_out);
endmodule

module count (
  input  in_1,
  output [3:0] out_2
);

  wire clock_1_out;
  wire [3:0] adder_1_out;

  Clock clock_1 (.out(clock_1_out));
  Adder #(.width(4)) adder_1 (.a(out_2), .b(4'b0001), .out(adder_1_out), .cin(1'b0));  // open: cout
  register register_1 (.in_1(adder_1_out), .out_4(out_2), .in_3(in_1), .in_2(clock_1_out));
endmodule

module register_3 (
  input  [3:0] in_1,
  input  in_2,
  input  in_3,
  output [3:0] out_4
);

  DCHU dchu_1 (.in_1(in_2), .in_2(in_1[0]), .in_3(in_3), .out_4(out_4[0]));  // open: out_5
  Dchufanes dchufanes_1 (.in_1(in_2), .in_2(in_1[1]), .in_3(in_3), .out_4(out_4[1]));  // open: out_5
  Dchufanes dchufanes_2 (.in_1(in_2), .in_2(in_1[2]), .in_3(in_3), .out_4(out_4[2]));  // open: out_5
  DCHU dchu_2 (.in_1(in_2), .in_2(in_1[3]), .in_3(in_3), .out_4(out_4[3]));  // open: out_5
endmodule

module countdown (
  input  [3:0] in_1,
  input  in_2,
  output [3:0] out_3
);

  wire clock_1_out;
  wire [3:0] mux_1_out_3, subtractor_1_out;

  Clock clock_1 (.out(clock_1_out));
  Subtractor #(.width(4)) subtractor_1 (.a(out_3), .b(in_1), .out(subtractor_1_out), .bin(1'b0));  // open: bout
  mux mux_1 (.in_1(subtractor_1_out), .out_3(mux_1_out_3), .in_2(out_3));
  register_3 register_3_1 (.in_1(mux_1_out_3), .in_2(clock_1_out), .in_3(in_2), .out_4(out_3));
endmodule

module mux (
  input  [3:0] in_1,
  input  [3:0] in_2,
  output [3:0] out_3
);

  wire and_1_out, and_2_out, and_3_out, and_4_out, and_5_out, and_6_out, and_7_out, and_8_out, not_1_out,
       or_1_out;

  or or_1 (or_1_out, in_2[0], in_2[1], in_2[2], in_2[3]);
  not not_1 (not_1_out, or_1_out);
  and and_1 (and_1_out, in_1[0], or_1_out);
  and and_2 (and_2_out, in_1[1], or_1_out);
  and and_3 (and_3_out, in_1[2], or_1_out);
  and and_4 (and_4_out, in_1[3], or_1_out);
  and and_5 (and_5_out, 1'b1, not_1_out);
  and and_6 (and_6_out, 1'b0, not_1_out);
  and and_7 (and_7_out, 1'b0, not_1_out);
  and and_8 (and_8_out, 1'b1, not_1_out);
  or or_2 (out_3[0], and_1_out, and_5_out);
  or or_3 (out_3[1], and_2_out, and_6_out);
  or or_4 (out_3[2], and_3_out, and_7_out);
  or or_5 (out_3[3], and_4_out, and_8_out);
endmodule

module Dchufanes (
  input  in_1,
  input  in_2,
  input  in_3,
  output out_4,
  output out_5
);

  wire dlatch_1_q, not_1_out;

  not not_1 (not_1_out, in_1);
  Dlatch dlatch_1 (.Q(dlatch_1_q), .in_1(not_1_out), .in_3(in_2), .in_2(in_3));  // open: nQ
  Dlatch dlatch_2 (.Q(out_4), .nQ(out_5), .in_1(in_1), .in_3(dlatch_1_q), .in_2(in_3));
endmodule

module tesr (
  input  clk,
  input  D,
  input  PRS,
  output out_4,
  output out_5
);

  wire dlatch_1_q, not_1_out;

  not not_1 (not_1_out, clk);
  Dlatch dlatch_1 (.Q(dlatch_1_q), .in_1(not_1_out), .in_3(D), .in_2(PRS));  // open: nQ
  Dlatch dlatch_2 (.Q(out_4), .nQ(out_5), .in_1(clk), .in_3(dlatch_1_q), .in_2(PRS));
endmodule

module test (
  input  CLK,
  input  D,
  input  SET,
  input  PRS,
  output out_5
);

  wire or_1_out;

  or or_1 (or_1_out, D, SET);
  tesr tesr_1 (.clk(CLK), .D(or_1_out), .PRS(PRS), .out_4(out_5));  // open: out_5
endmodule

module Dlatch2 (
  input  in_1,
  input  in_2,
  input  in_3,
  output Q,
  output nQ
);

  wire and_1_out, and_2_out, and_3_out, not_1_out, not_2_out, or_1_out;

  not not_1 (not_1_out, in_3);
  not not_2 (not_2_out, in_2);
  and and_1 (and_1_out, in_1, not_1_out);
  and and_2 (and_2_out, in_1, in_3);
  and and_3 (and_3_out, in_2, and_1_out);
  or or_1 (or_1_out, and_2_out, not_2_out);
  \双稳态  \u_双稳态_1  (.R(and_3_out), .S(or_1_out), .Q(Q), .nQ(nQ));
endmodule

module DCHU (
  input  in_1,
  input  in_2,
  input  in_3,
  output out_4,
  output out_5
);

  wire dlatch2_1_q, not_1_out;

  not not_1 (not_1_out, in_1);
  Dlatch2 dlatch2_1 (.in_1(not_1_out), .in_2(in_3), .in_3(in_2), .Q(dlatch2_1_q));  // open: nQ
  Dlatch2 dlatch2_2 (.in_1(in_1), .in_2(in_3), .in_3(dlatch2_1_q), .Q(out_4), .nQ(out_5));
endmodule

module \高电平有效  (
  input  in_1,
  input  in_2,
  input  in_3,
  output Q,
  output nQ
);

  wire and_1_out, and_2_out, not_1_out, or_1_out, or_2_out;

  not not_1 (not_1_out, or_1_out);
  or or_1 (or_1_out, in_2, in_3);
  and and_1 (and_1_out, in_1, not_1_out);
  and and_2 (and_2_out, in_1, or_1_out);
  or or_2 (or_2_out, in_2, and_1_out);
  \双稳态  \u_双稳态_1  (.R(or_2_out), .S(and_2_out), .Q(Q), .nQ(nQ));
endmodule

module t1 (
  input  in_1,
  input  in_2,
  input  in_3,
  output Q,
  output nQ
);

  wire and_1_out, and_2_out, and_3_out, not_1_out, not_2_out, not_3_out, not_4_out, or_1_out;

  not not_1 (not_1_out, in_3);
  or or_1 (or_1_out, in_1, not_1_out);
  and and_1 (and_1_out, in_2, in_3);
  not not_2 (not_2_out, and_1_out);
  and and_2 (and_2_out, or_1_out, and_1_out);
  and and_3 (and_3_out, or_1_out, not_2_out);
  not not_3 (not_3_out, and_2_out);
  not not_4 (not_4_out, and_3_out);
  nand nand_1 (Q, not_3_out, nQ);
  nand nand_2 (nQ, Q, not_4_out);
endmodule

module t2 (
  input  CLK,
  input  D,
  output Q,
  output nQ
);

  wire and_1_out, and_2_out, not_1_out;

  and and_1 (and_1_out, CLK, not_1_out);
  not not_1 (not_1_out, D);
  and and_2 (and_2_out, CLK, D);
  \双稳态  \u_双稳态_1  (.R(and_1_out), .S(and_2_out), .Q(Q), .nQ(nQ));
endmodule
