// Logisim project exper6.circ as structural Verilog: 1 circuit, main circuit main
module main (
  input  in_1,
  input  in_2,
  input  a,
  input  _1,
  output output1,
  output output2,
  output output3,
  output \引脚B ,
  output \引脚A 
);

  wire bitselector_2_out, buffer_1_out, buffer_2_out, clk_out, decoder_1_out1, decoder_1_out2,
       decoder_1_out3, decoder_2_out1, decoder_2_out2, decoder_2_out3, decoder_3_out1, decoder_3_out2,
       decoder_3_out3;
  wire [0:0] bitselector_1_out;
  wire [1:0] d_ff_1_q;

  Clock clk (.out(clk_out));
  BitSelector #(.width(2)) bitselector_1 (.in({a, output1}), .out(bitselector_1_out[0]), .sel(1'b0));
  RAM #(.addrWidth(2), .dataWidth(1)) ram_1 (
    .addr({_1, bitselector_1_out[0]}), .data(d_ff_1_q[1]));  // open: sel, clk, ld, clr
  D_Flip_Flop d_ff_1 (.clk(clk_out), .D(d_ff_1_q[1]), .Q(d_ff_1_q[0]));  // open: Qn, preset, en, reset
  BitSelector #(.width(2)) bitselector_2 (.in(d_ff_1_q), .out(bitselector_2_out), .sel(1'b1));
  assign output1 = decoder_1_out1 ? in_1 : 1'bz;  // Controlled_Buffer controlled_buffer_1
  assign output1 = decoder_1_out2 ? in_2 : 1'bz;  // Controlled_Buffer controlled_buffer_2
  assign output1 = decoder_1_out3 ? bitselector_2_out : 1'bz;  // Controlled_Buffer controlled_buffer_3
  Decoder #(.select(2)) decoder_1 (
    .out1(decoder_1_out1), .out2(decoder_1_out2), .out3(decoder_1_out3), .sel(2'b11));  // open: out0, en
  Decoder #(.select(2)) decoder_2 (
    .out1(decoder_2_out1), .out2(decoder_2_out2), .out3(decoder_2_out3), .sel(2'b11));  // open: out0, en
  assign output2 = decoder_2_out1 ? in_1 : 1'bz;  // Controlled_Buffer controlled_buffer_4
  assign output2 = decoder_2_out2 ? in_2 : 1'bz;  // Controlled_Buffer controlled_buffer_5
  assign output2 = decoder_2_out3 ? bitselector_2_out : 1'bz;  // Controlled_Buffer controlled_buffer_6
  Decoder #(.select(2)) decoder_3 (
    .out1(decoder_3_out1), .out2(decoder_3_out2), .out3(decoder_3_out3), .sel(2'b01));  // open: out0, en
  assign output3 = decoder_3_out1 ? in_1 : 1'bz;  // Controlled_Buffer controlled_buffer_7
  assign output3 = decoder_3_out2 ? in_2 : 1'bz;  // Controlled_Buffer controlled_buffer_8
  assign output3 = decoder_3_out3 ? bitselector_2_out : 1'bz;  // Controlled_Buffer controlled_buffer_9
  buf buffer_1 (buffer_1_out, \引脚B );
  assign \引脚B  = 1'b1 ? output2 : 1'bz;  // Controlled_Buffer controlled_buffer_10
  buf buffer_2 (buffer_2_out, \引脚A );
  assign \引脚A  = 1'b1 ? output3 : 1'bz;  // Controlled_Buffer controlled_buffer_11
endmodule
