// Logisim project exper8.circ as structural Verilog: 3 circuits, main circuit main
module main (
  input  in_1,
  input  in_2,
  output out_3
);

  wire d_ff_1_q, d_ff_2_q;

  D_Flip_Flop d_ff_1 (.clk(in_1), .D(in_2), .Q(d_ff_1_q));  // open: Qn, preset, en, reset
  D_Flip_Flop d_ff_2 (.clk(in_1), .D(d_ff_1_q), .Q(d_ff_2_q));  // open: Qn, preset, en, reset
  xor xor_1 (out_3, d_ff_2_q, d_ff_1_q);
endmodule

module _8_2 (
  input  in_1,
  input  in_2,
  input  in_3,
  output [3:0] out_4
);

  wire main_1_out_3;
  wire [3:0] adder_1_out, multiplexer_1_out;

  Adder #(.width(4)) adder_1 (.a(out_4), .b(4'b0001), .out(adder_1_out));  // open: cin, cout
  main main_1 (.in_1(in_2), .in_2(in_3), .out_3(main_1_out_3));
  Multiplexer #(.width(4)) multiplexer_1 (
    .in0(out_4), .in1(adder_1_out), .out(multiplexer_1_out), .sel(main_1_out_3));  // open: en
  Register #(.width(4)) register_1 (.D(multiplexer_1_out), .Q(out_4), .clk(in_2), .clr(in_1));  // open: en
endmodule

module _8_22 (
  input  in_1,
  input  in_2,
  output [3:0] out_3
);

  wire clock_1_out;

  Clock clock_1 (.out(clock_1_out));
  _8_2 u_8_2_1 (.in_2(clock_1_out), .in_3(in_2), .out_4(out_3), .in_1(in_1));
endmodule
